// Logisim project ALU_4_bits_Bloc.circ as structural Verilog: 16 circuits, main circuit Aritmetico
module main (
  input  A3,
  input  in_2,
  input  in_3,
  input  A0,
  input  B3,
  input  in_6,
  input  in_7,
  input  B0,
  input  CyBwi,
  input  S2,
  input  S1,
  input  S0,
  output R0,
  output out_14,
  output out_15,
  output R3,
  output OV,
  output LTE,
  output CyBwo
);

  ALU alu_1 (
    .CyBwi(CyBwi), .A0(A0), .A1(in_3), .A2(in_2), .A3(A3), .B0(B0), .B1(in_7), .B2(in_6), .B3(B3), .S1(S1),
    .S2(S2), .R0(R0), .R1(out_14), .R2(out_15), .R3(R3), .OV(OV), .LTE(LTE), .CyBwo(CyBwo), .S0(S0));
endmodule

module ALU (
  input  CyBwi,
  input  A0,
  input  A1,
  input  A2,
  input  A3,
  input  B0,
  input  B1,
  input  B2,
  input  B3,
  input  S0,
  input  S1,
  input  S2,
  output R0,
  output R1,
  output R2,
  output R3,
  output OV,
  output LTE,
  output CyBwo
);

  wire aritmetico_1_cybwa, aritmetico_1_ra0, aritmetico_1_ra1, aritmetico_1_ra2, aritmetico_1_ra3,
       logicoshift_1_ls0, logicoshift_1_ls1, logicoshift_1_ls2, logicoshift_1_ls3, logicoshift_1_shcy,
       mux_2x1_1_out_5;

  Aritmetico aritmetico_1 (
    .CyBwi(CyBwi), .A0(A0), .A1(A1), .A2(A2), .A3(A3), .B0(B0), .B1(B1), .B2(B2), .B3(B3), .S1(S1),
    .RA0(aritmetico_1_ra0), .RA1(aritmetico_1_ra1), .RA2(aritmetico_1_ra2), .RA3(aritmetico_1_ra3),
    .CyBwA(aritmetico_1_cybwa), .OV(OV), .LTE(LTE), .S0(S0));
  LogicoShift logicoshift_1 (
    .A0(A0), .A1(A1), .A2(A2), .A3(A3), .B0(B0), .B1(B1), .B2(B2), .B3(B3), .SnL(S0),
    .LS0(logicoshift_1_ls0), .LS1(logicoshift_1_ls1), .LS2(logicoshift_1_ls2), .LS3(logicoshift_1_ls3),
    .ShCy(logicoshift_1_shcy));
  Mux_2x4 mux_2x4_1 (
    .a0(aritmetico_1_ra0), .b0(logicoshift_1_ls0), .a1(aritmetico_1_ra1), .b1(logicoshift_1_ls1),
    .a2(aritmetico_1_ra2), .b2(logicoshift_1_ls2), .a3(aritmetico_1_ra3), .b3(logicoshift_1_ls3),
    .S(mux_2x1_1_out_5), .y0(R0), .y1(R1), .y2(R2), .y3(R3));
  Mux_2x1 mux_2x1_1 (.I0(aritmetico_1_cybwa), .I1(logicoshift_1_shcy), .S(S2), .Y(CyBwo), .out_5(mux_2x1_1_out_5));
endmodule

module Aritmetico (
  input  CyBwi,
  input  A0,
  input  A1,
  input  A2,
  input  A3,
  input  B0,
  input  B1,
  input  B2,
  input  B3,
  input  S0,
  input  S1,
  output RA0,
  output RA1,
  output RA2,
  output RA3,
  output CyBwA,
  output LTE,
  output OV
);

  wire adder4bit_1_c4, btrans_1_bt0, btrans_1_bt1, btrans_1_bt2, btrans_1_bt3, cybw_1_c0;

  CyBw cybw_1 (.CyBwi(CyBwi), .S0(S0), .S1(S1), .C0(cybw_1_c0));
  BTrans btrans_1 (
    .B0(B0), .B1(B1), .B2(B2), .B3(B3), .BT0(btrans_1_bt0), .BT1(btrans_1_bt1), .BT2(btrans_1_bt2),
    .BT3(btrans_1_bt3), .SnA(S0));
  Adder4bit adder4bit_1 (
    .C0(cybw_1_c0), .A0(A0), .B0(btrans_1_bt0), .A1(A1), .B1(btrans_1_bt1), .A2(A2), .B2(btrans_1_bt2),
    .A3(A3), .B3(btrans_1_bt3), .S0(RA0), .S1(RA1), .S2(RA2), .S3(RA3), .C4(adder4bit_1_c4));
  overflaw overflaw_1 (.A3(A3), .B3(btrans_1_bt3), .S3(RA3), .OV(OV));
  C4T c4t_1 (.C4(adder4bit_1_c4), .SnA(S0), .CyBwA(CyBwA));
  LTE lte_1 (.R0(RA0), .R1(RA1), .R2(RA2), .R3(RA3), .OV(OV), .LTE(LTE));
endmodule

module Adder4bit (
  input  C0,
  input  A0,
  input  B0,
  input  A1,
  input  B1,
  input  A2,
  input  B2,
  input  A3,
  input  B3,
  output S0,
  output S1,
  output S2,
  output S3,
  output C4
);

  wire fulladder_1_ci_1, fulladder_2_ci_1, fulladder_3_ci_1;

  FullAdder fulladder_1 (.ai(A0), .bi(B0), .ci(C0), .si(S0), .ci_1(fulladder_1_ci_1));
  FullAdder fulladder_2 (.ai(A1), .bi(B1), .ci(fulladder_1_ci_1), .si(S1), .ci_1(fulladder_2_ci_1));
  FullAdder fulladder_3 (.ai(A2), .bi(B2), .ci(fulladder_2_ci_1), .si(S2), .ci_1(fulladder_3_ci_1));
  FullAdder fulladder_4 (.ai(A3), .bi(B3), .ci(fulladder_3_ci_1), .si(S3), .ci_1(C4));
endmodule

module FullAdder (
  input  ai,
  input  bi,
  input  ci,
  output si,
  output ci_1
);

  wire and_1_out, and_2_out, and_3_out, or_1_out, xor_1_out;

  and and_1 (and_1_out, ci, ai);
  and and_2 (and_2_out, ci, bi);
  and and_3 (and_3_out, ai, bi);
  xor xor_1 (xor_1_out, ai, bi);
  or or_1 (or_1_out, and_1_out, and_2_out);
  xor xor_2 (si, xor_1_out, ci);
  or or_2 (ci_1, or_1_out, and_3_out);
endmodule

module overflaw (
  input  A3,
  input  B3,
  input  S3,
  output OV
);

  wire and_1_out, and_2_out;

  and and_1 (and_1_out, A3, B3, ~S3);  // AND_Gate
  and and_2 (and_2_out, ~A3, ~B3, S3);  // AND_Gate
  or or_1 (OV, and_1_out, and_2_out);
endmodule

module LTE (
  input  R0,
  input  R1,
  input  R2,
  input  R3,
  input  OV,
  output LTE
);

  wire and_1_out, and_2_out, and_3_out, or_1_out;

  and and_1 (and_1_out, ~R0, ~R1, ~R2, ~R3);  // AND_Gate
  and and_2 (and_2_out, ~R3, ~OV);  // AND_Gate
  and and_3 (and_3_out, R3, OV);
  or or_1 (or_1_out, and_2_out, and_3_out);
  or or_2 (LTE, and_1_out, or_1_out);
endmodule

module LogicoShift (
  input  A0,
  input  A1,
  input  A2,
  input  A3,
  input  B0,
  input  B1,
  input  B2,
  input  B3,
  input  SnL,
  output LS0,
  output LS1,
  output LS2,
  output LS3,
  output ShCy
);

  wire logico_1_nor0, logico_1_nor1, logico_1_nor2, logico_1_nor3, logicshiftleft_1_lsl0,
       logicshiftleft_1_lsl1, logicshiftleft_1_lsl2, logicshiftleft_1_lsl3;

  Logico logico_1 (
    .A0(A0), .B0(B0), .A1(A1), .B1(B1), .A2(A2), .B2(B2), .A3(A3), .B3(B3), .NOR0(logico_1_nor0),
    .NOR1(logico_1_nor1), .NOR2(logico_1_nor2), .NOR3(logico_1_nor3));
  LogicShiftLeft logicshiftleft_1 (
    .A0(A0), .A1(A1), .A2(A2), .A3(A3), .S1(B1), .S0(B0), .LSL0(logicshiftleft_1_lsl0),
    .LSL1(logicshiftleft_1_lsl1), .LSL2(logicshiftleft_1_lsl2), .LSL3(logicshiftleft_1_lsl3), .LSLCy(ShCy));
  Mux_2x4 mux_2x4_1 (
    .a0(logico_1_nor0), .b0(logicshiftleft_1_lsl0), .a1(logico_1_nor1), .b1(logicshiftleft_1_lsl1),
    .a2(logico_1_nor2), .b2(logicshiftleft_1_lsl2), .a3(logico_1_nor3), .b3(logicshiftleft_1_lsl3), .S(SnL),
    .y0(LS0), .y1(LS1), .y2(LS2), .y3(LS3));
endmodule

module Logico (
  input  A0,
  input  B0,
  input  A1,
  input  B1,
  input  A2,
  input  B2,
  input  A3,
  input  B3,
  output NOR0,
  output NOR1,
  output NOR2,
  output NOR3
);

  nor nor_1 (NOR0, A0, B0);
  nor nor_2 (NOR1, A1, B1);
  nor nor_3 (NOR2, A2, B2);
  nor nor_4 (NOR3, A3, B3);
endmodule

// 2
module LogicShiftLeft (
  input  A0,
  input  A1,
  input  A2,
  input  A3,
  input  S1,
  input  S0,
  output LSL0,
  output LSL1,
  output LSL2,
  output LSL3,
  output LSLCy
);

  wire mux_4x1_2_out_8, mux_4x1_2_out_9, mux_4x1_3_out_8, mux_4x1_3_out_9, mux_4x1_4_out_8, mux_4x1_4_out_9,
       mux_4x1_5_out_8, mux_4x1_5_out_9;

  Mux_4x1 mux_4x1_1 (
    .I0(A0), .I1(1'b0), .I2(1'b0), .I3(1'b0), .S0(mux_4x1_2_out_8), .S1(mux_4x1_2_out_9), .Y(LSL0));  // open: out_8, out_9
  Mux_4x1 mux_4x1_2 (
    .I0(A1), .I1(A0), .I2(1'b0), .I3(1'b0), .S0(mux_4x1_3_out_8), .S1(mux_4x1_3_out_9), .Y(LSL1),
    .out_8(mux_4x1_2_out_8), .out_9(mux_4x1_2_out_9));
  Mux_4x1 mux_4x1_3 (
    .I0(A2), .I1(A1), .I2(A0), .I3(1'b0), .S0(mux_4x1_4_out_8), .S1(mux_4x1_4_out_9), .Y(LSL2),
    .out_8(mux_4x1_3_out_8), .out_9(mux_4x1_3_out_9));
  Mux_4x1 mux_4x1_4 (
    .I0(A3), .I1(A2), .I2(A1), .I3(A0), .S0(mux_4x1_5_out_8), .S1(mux_4x1_5_out_9), .Y(LSL3),
    .out_8(mux_4x1_4_out_8), .out_9(mux_4x1_4_out_9));
  Mux_4x1 mux_4x1_5 (
    .I0(A0), .I1(A3), .I2(A2), .I3(A1), .S0(S0), .S1(S1), .Y(LSLCy), .out_8(mux_4x1_5_out_8),
    .out_9(mux_4x1_5_out_9));
endmodule

module Mux_4x1 (
  input  I0,
  input  I1,
  input  I2,
  input  I3,
  input  S0,
  input  S1,
  output Y,
  output out_8,
  output out_9
);

  wire and_1_out, and_2_out, and_3_out, and_4_out;

  and and_1 (and_1_out, I0, ~S0, ~S1);  // AND_Gate
  and and_2 (and_2_out, I1, S0, ~S1);  // AND_Gate
  and and_3 (and_3_out, I2, ~S0, S1);  // AND_Gate
  and and_4 (and_4_out, I3, S0, S1);
  or or_1 (Y, and_1_out, and_2_out, and_3_out, and_4_out);

  assign out_8 = S0;
  assign out_9 = S1;
endmodule

module Mux_2x1 (
  input  I0,
  input  I1,
  input  S,
  output Y,
  output out_5
);

  wire and_1_out, and_2_out;

  and and_1 (and_1_out, I0, ~S);  // AND_Gate
  and and_2 (and_2_out, I1, S);
  or or_1 (Y, and_1_out, and_2_out);

  assign out_5 = S;
endmodule

module Mux_2x4 (
  input  a0,
  input  b0,
  input  a1,
  input  b1,
  input  a2,
  input  b2,
  input  a3,
  input  b3,
  input  S,
  output y0,
  output y1,
  output y2,
  output y3
);

  wire and_1_out, and_2_out, and_3_out, and_4_out, and_5_out, and_6_out, and_7_out, and_8_out;

  and and_1 (and_1_out, a0, ~S);  // AND_Gate
  and and_2 (and_2_out, b0, S);
  and and_3 (and_3_out, a1, ~S);  // AND_Gate
  and and_4 (and_4_out, b1, S);
  and and_5 (and_5_out, a2, ~S);  // AND_Gate
  and and_6 (and_6_out, b2, S);
  and and_7 (and_7_out, a3, ~S);  // AND_Gate
  and and_8 (and_8_out, b3, S);
  or or_1 (y0, and_1_out, and_2_out);
  or or_2 (y1, and_3_out, and_4_out);
  or or_3 (y2, and_5_out, and_6_out);
  or or_4 (y3, and_7_out, and_8_out);
endmodule

// C0T
module CyBw (
  input  CyBwi,
  input  S0,
  input  S1,
  output C0
);

  wire and_1_out, and_2_out;

  and and_1 (and_1_out, ~CyBwi, S0, S1);  // AND_Gate
  and and_2 (and_2_out, CyBwi, ~S0, S1);  // AND_Gate
  or or_1 (C0, and_1_out, and_2_out);
endmodule

// BT
module BTrans (
  input  B0,
  input  B1,
  input  B2,
  input  B3,
  input  SnA,
  output BT0,
  output BT1,
  output BT2,
  output BT3
);

  xor xor_1 (BT0, B0, SnA);
  xor xor_2 (BT1, B1, SnA);
  xor xor_3 (BT2, B2, SnA);
  xor xor_4 (BT3, B3, SnA);
endmodule

module C4T (
  input  C4,
  input  SnA,
  output CyBwA
);

  xor xor_1 (CyBwA, C4, SnA);
endmodule
